// Logisim project hassan_jaffal.circ as structural Verilog: 2 circuits, main circuit hassan jaffal
module hassan_jaffal (
  input  x,
  input  y,
  input  z,
  output a,
  output b,
  output c,
  output d,
  output e,
  output f,
  output g
);

  wire not_2_out, not_3_out, x_prime___y_prime_z_prime_out, x_prime_y_prime_out, x_prime_z_out,
       x_y_z_prime_out, xz_prime_out, y___z_out;

  not not_1 (f, x);
  not not_2 (not_2_out, y);
  not not_3 (not_3_out, z);
  or y___z (y___z_out, y, z);
  and x_prime_y_prime (x_prime_y_prime_out, f, not_2_out);
  and x_prime_z (x_prime_z_out, z, f);
  and x_y_z_prime (x_y_z_prime_out, x, y, not_3_out);
  and xz_prime (xz_prime_out, x, not_3_out);
  and x_prime___y_prime_z_prime (x_prime___y_prime_z_prime_out, not_3_out, not_2_out);
  or x_prime___z_prime (c, not_3_out, f);
  and y_z_prime (d, y, not_3_out);
  or xz_prime___x_prime_z__x_prime_y_prime (e, x_prime_z_out, xz_prime_out, x_prime_y_prime_out);
  or x_prime___y_prime_z_prime_2 (g, f, x_prime___y_prime_z_prime_out);
  and x_prime__y_z (a, f, y___z_out);
  or xyz_prime___x_prime_y_prime__x_prime_z (b, x_prime_y_prime_out, x_prime_z_out, x_y_z_prime_out);
endmodule

module main (
);

  wire a, a1, a2, a3, a4, b, b1, b2, b3, b4, c, c1, c2, c3, c4, clock_1_out, d, d1, d2, d3, d4, e, e1, e2,
       e3, e4, f, f1, f2, f3, f4, g, g1, g2, g3, g4, hassan_jaffal_1_a, hassan_jaffal_1_b, hassan_jaffal_1_c,
       hassan_jaffal_1_d, hassan_jaffal_1_e, hassan_jaffal_1_f, hassan_jaffal_1_g, hassan_jaffal_2_a,
       hassan_jaffal_2_b, hassan_jaffal_2_c, hassan_jaffal_2_d, hassan_jaffal_2_e, hassan_jaffal_2_f,
       hassan_jaffal_2_g, hassan_jaffal_3_a, hassan_jaffal_3_b, hassan_jaffal_3_c, hassan_jaffal_3_d,
       hassan_jaffal_3_e, hassan_jaffal_3_f, hassan_jaffal_3_g;
  wire [2:0] adder_1_out, adder_2_out, adder_3_out, adder_4_out, adder_5_out, adder_6_out, adder_7_out,
       counter_1_q;

  Clock clock_1 (.out(clock_1_out));
  Counter #(.width(3), .max('h7)) counter_1 (.Q(counter_1_q), .clk(clock_1_out));  // open: load, D, count, carry, clr
  hassan_jaffal hassan_jaffal_1 (
    .x(counter_1_q[2]), .y(counter_1_q[1]), .z(counter_1_q[0]), .a(hassan_jaffal_1_a), .b(hassan_jaffal_1_b),
    .c(hassan_jaffal_1_c), .d(hassan_jaffal_1_d), .e(hassan_jaffal_1_e), .f(hassan_jaffal_1_f),
    .g(hassan_jaffal_1_g));
  Adder #(.width(3)) adder_1 (.a(counter_1_q), .b(3'b001), .out(adder_1_out));  // open: cin, cout
  hassan_jaffal hassan_jaffal_2 (
    .x(adder_1_out[2]), .y(adder_1_out[1]), .z(adder_1_out[0]), .a(hassan_jaffal_2_a), .b(hassan_jaffal_2_b),
    .c(hassan_jaffal_2_c), .d(hassan_jaffal_2_d), .e(hassan_jaffal_2_e), .f(hassan_jaffal_2_f),
    .g(hassan_jaffal_2_g));
  Adder #(.width(3)) adder_2 (.a(adder_1_out), .b(3'b001), .out(adder_2_out));  // open: cin, cout
  Adder #(.width(3)) adder_3 (.a(adder_2_out), .b(3'b001), .out(adder_3_out));  // open: cin, cout
  Adder #(.width(3)) adder_4 (.a(adder_3_out), .b(3'b001), .out(adder_4_out));  // open: cin, cout
  Adder #(.width(3)) adder_5 (.a(adder_4_out), .b(3'b001), .out(adder_5_out));  // open: cin, cout
  Adder #(.width(3)) adder_6 (.a(adder_5_out), .b(3'b001), .out(adder_6_out));  // open: cin, cout
  Adder #(.width(3)) adder_7 (.a(adder_6_out), .b(3'b001), .out(adder_7_out));  // open: cin, cout
  hassan_jaffal hassan_jaffal_3 (
    .x(adder_2_out[2]), .y(adder_2_out[1]), .z(adder_2_out[0]), .a(hassan_jaffal_3_a), .b(hassan_jaffal_3_b),
    .c(hassan_jaffal_3_c), .d(hassan_jaffal_3_d), .e(hassan_jaffal_3_e), .f(hassan_jaffal_3_f),
    .g(hassan_jaffal_3_g));
  hassan_jaffal hassan_jaffal_4 (
    .x(adder_3_out[2]), .y(adder_3_out[1]), .z(adder_3_out[0]), .a(a), .b(b), .c(c), .d(d), .e(e), .f(f),
    .g(g));
  hassan_jaffal hassan_jaffal_5 (
    .x(adder_4_out[2]), .y(adder_4_out[1]), .z(adder_4_out[0]), .a(a1), .b(b1), .c(c1), .d(d1), .e(e1),
    .f(f1), .g(g1));
  hassan_jaffal hassan_jaffal_6 (
    .x(adder_5_out[0]), .y(adder_5_out[1]), .z(adder_5_out[2]), .a(a2), .b(b2), .c(c2), .d(d2), .e(e2),
    .f(f2), .g(g2));
  hassan_jaffal hassan_jaffal_7 (
    .x(adder_6_out[2]), .y(adder_6_out[1]), .z(adder_6_out[0]), .a(a3), .b(b3), .c(c3), .d(d3), .e(e3),
    .f(f3), .g(g3));
  _7_Segment_Display u_7_segment_display_1 (
    .g(hassan_jaffal_1_g), .f(hassan_jaffal_1_f), .a(hassan_jaffal_1_a), .b(hassan_jaffal_1_b),
    .e(hassan_jaffal_1_e), .d(hassan_jaffal_1_d), .c(hassan_jaffal_1_c));  // open: dp
  hassan_jaffal hassan_jaffal_8 (
    .x(adder_7_out[2]), .y(adder_7_out[1]), .z(adder_7_out[0]), .a(a4), .b(b4), .c(c4), .d(d4), .e(e4),
    .f(f4), .g(g4));
  _7_Segment_Display u_7_segment_display_2 (
    .g(hassan_jaffal_2_g), .f(hassan_jaffal_2_f), .a(hassan_jaffal_2_a), .b(hassan_jaffal_2_b),
    .e(hassan_jaffal_2_e), .d(hassan_jaffal_2_d), .c(hassan_jaffal_2_c));  // open: dp
  _7_Segment_Display u_7_segment_display_3 (
    .g(hassan_jaffal_3_g), .f(hassan_jaffal_3_f), .a(hassan_jaffal_3_a), .b(hassan_jaffal_3_b),
    .e(hassan_jaffal_3_e), .d(hassan_jaffal_3_d), .c(hassan_jaffal_3_c));  // open: dp
  _7_Segment_Display u_7_segment_display_4 (.g(g), .f(f), .a(a), .b(b), .e(e), .d(d), .c(c));  // open: dp
  _7_Segment_Display u_7_segment_display_5 (.g(g1), .f(f1), .a(a1), .b(b1), .e(e1), .d(d1), .c(c1));  // open: dp
  _7_Segment_Display u_7_segment_display_6 (.g(g2), .f(f2), .a(a2), .b(b2), .e(e2), .d(d2), .c(c2));  // open: dp
  _7_Segment_Display u_7_segment_display_7 (.g(g3), .f(f3), .a(a3), .b(b3), .e(e3), .d(d3), .c(c3));  // open: dp
endmodule
